# Fritzing sketch FilPiloteTeleInfoV2 (saved by Fritzing 0.9.2b)
circuit board: 12.0703cm x 8.83542cm
breadboards: 3

parts:
  U1 = MOC3031-M [package=dil06]
  U3 = MOC3031-M [package=dil06]
  D1 = Rectifier Diode [part_number=1N4001 package="300 mil [THT]"]
  D2 = Rectifier Diode [part_number=1N4001 package="300 mil [THT]"]
  D3 = Rectifier Diode [part_number=1N4001 package="300 mil [THT]"]
  R1 = Resistor [tolerance=±5% resistance=470 package=THT]
  R2 = Resistor [tolerance=±5% resistance=470 package=THT]
  R3 = Resistor [tolerance=±5% resistance=470 package=THT]
  Part1 = Arduino Nano (Rev3.0)
  R4 = Resistor [tolerance=±5% resistance=330 package=THT]
  R5 = Resistor [tolerance=±5% resistance=330 package=THT]
  LED2 = LED - 5mm [color="Red (633nm)" package="5 mm [THT]"]
  LED3 = LED - 5mm [color="Red (633nm)" package="5 mm [THT]"]
  R6 = Resistor [tolerance=±5% resistance=330 package=THT]
  LED1 = LED - 5mm [color="Red (633nm)" package="5 mm [THT]"]
  U4 = MOC3031-M [package=dil06]
  R7 = Resistor [tolerance=±5% resistance=470 package=THT]
  LED4 = LED - 5mm [color="Red (633nm)" package="5 mm [THT]"]
  R8 = Resistor [tolerance=±5% resistance=330 package=THT]
  J2 = screw terminal, 4 pins
  D4 = Rectifier Diode [part_number=1N4001 package="300 mil [THT]"]
  J3 = Screw terminal - 2 pins [package=THT]
  K1 = Relay [part_number=FRS1B-S package=THT]
  J1 = Screw terminal - 2 pins [package=THT]
  U2 = MOC3031-M [package=dil06]
  LED7 = LED - 5mm [color="Red (633nm)" package="5 mm [THT]"]
  J4 = Screw terminal - 2 pins [package=THT]
  R12 = Resistor [tolerance=±5% resistance=1.2k package=THT]
  R13 = Resistor [tolerance=±5% resistance=4.7k package=THT]
  J5 = female pin header, 2 pins [form="♀ (female)"]
  J6 = female pin header, 4 pins [form="♀ (female)"]
  U5 = TLP621 [package=THT]
  R11 = Resistor [tolerance=±5% resistance=220 package=THT]

nets:
  N1: U1.1, R1.Pin_1
  N2: U1.2, U3.2, Part1.GND, R4.Pin_0, R5.Pin_0, R6.Pin_0, U4.2, R8.Pin_0, K1.COIL2, U2.2, U5.Pin_1, R11.Pin_0
  N3: U1.4, D3.cathode
  N4: U1.6, U3.6, U4.6, J1.pin1, U2.6
  N5: U3.1, R3.Pin_1
  N6: U3.4, D1.cathode
  N7: D1.anode, J2.pin3
  N8: D2.cathode, U2.4
  N9: D2.anode, J2.pin2
  N10: D3.anode, J2.pin1
  N11: R1.Pin_0, Part1.D3, LED1.anode
  N12: R2.Pin_0, Part1.D4, LED2.anode
  N13: R2.Pin_1, U2.1
  N14: R3.Pin_0, Part1.D5, LED3.anode
  N15: Part1.D2, R13.Pin_0, U5.Pin_2
  N16: Part1.D6, R7.Pin_0, LED4.anode
  N17: Part1.D7, LED7.anode
  N18: Part1.D8, K1.COIL1
  N19: Part1.D9, J6.pin4
  N20: Part1.D10, J6.pin3
  N21: Part1.D11/MOSI, J6.pin2
  N22: Part1.D12/MISO, J6.pin1
  N23: Part1.5V, R13.Pin_1
  N24: Part1.3V3, J5.pin1
  N25: Part1.D13/SCK, J5.pin2
  N26: R4.Pin_1, LED1.cathode
  N27: R5.Pin_1, LED2.cathode
  N28: LED3.cathode, R6.Pin_1
  N29: U4.1, R7.Pin_1
  N30: U4.4, D4.cathode
  N31: LED4.cathode, R8.Pin_1
  N32: J2.pin4, D4.anode
  N33: J3.pin1, K1.A
  N34: J3.pin2, K1.C1, K1.C2
  N35: LED7.cathode, R11.Pin_1
  N36: J4.pin1, U5.Pin_4
  N37: J4.pin2, R12.Pin_0
  N38: R12.Pin_1, U5.Pin_3
