# Fritzing sketch Temp_TransmiterV5 (saved by Fritzing 0.9.2b)
circuit board: 8.3cm x 5.4cm
breadboards: 1

parts:
  Part1 = Arduino Nano (Rev3.0)
  R1 = Resistor [tolerance=±5% resistance=10k package=THT]
  Part2 = NRF24L01
  DHT22 = Humidity and Temperature Sensor RHT03

nets:
  GND: Part1.GND, Part2.GND, DHT22.GND_1
  N1: Part1.D2, R1.Pin_0, DHT22.Data-signal
  N2: Part1.D9, Part2.CE
  N3: Part1.D10, Part2.CSN
  N4: Part1.D11/MOSI, Part2.MOSI
  N5: Part1.D12/MISO, Part2.MISO
  5V: Part1.5V, R1.Pin_1, DHT22.Vcc
  3V3: Part1.3V3, Part2.VCC
  N6: Part1.D13/SCK, Part2.SCK

notes:
  Temp Sensor
  Temp. Sensor A.Plessis
  NRF24
  R1
  DHT22
